# Fritzing sketch robot (saved by Fritzing 0.9.9b)

parts:
  Часть1 = Arduino Uno (Rev3)
  Часть5 = Arduino Cellular Shield
  M8 = DC Motor
  M9 = DC Motor
  M10 = DC Motor
  M11 = DC Motor
  M12 = DC Motor
  M13 = DC Motor
  VCC3 = Battery
  L298N1 = L298N DC motor driver
  L298N2 = L298N DC motor driver
  L298N3 = L298N DC motor driver
  PWM1 = PCA9685 16x12-bit PWM Breakout
  VCC4 = Battery
  M14 = fc-51 [package=THT]
  M15 = fc-51 [package=THT]
  M16 = fc-51 [package=THT]
  M17 = fc-51 [package=THT]

nets:
  N1: Часть1.A4/SDA, PWM1.no_name_yet#504
  N2: Часть1.A5/SCL, PWM1.no_name_yet#503
  N3: Часть1.D8, M14.pin1
  N4: Часть1.D9_PWM, L298N2.ENA
  N5: Часть1.D10_PWM/SS, L298N1.ENB
  N6: Часть1.D11_PWM/MOSI, L298N1.ENA
  N7: Часть1.D12/MISO, Часть5.TX-O
  N8: Часть1.D13/SCK, Часть5.RX-I
  N9: Часть1.GND, PWM1.no_name_yet#501, VCC4.-, M14.pin2, M15.pin2, M16.pin2, M17.pin2
  N10: Часть1.D2, M17.pin1
  N11: Часть1.D3_PWM, L298N3.ENB
  N12: Часть1.D4, M15.pin1
  N13: Часть1.D5_PWM, L298N3.ENA
  N14: Часть1.D6_PWM, L298N2.ENB
  N15: Часть1.D7, M16.pin1
  N16: Часть1.5V, PWM1.no_name_yet#505, M14.pin3, M15.pin3, M16.pin3, M17.pin3
  N17: Часть1.VIN, VCC4.+
  N18: M8.pin_1, L298N1.OUT2
  N19: M8.pin_2, L298N1.OUT1
  N20: M9.pin_1, L298N1.OUT4
  N21: M9.pin_2, L298N1.OUT3
  N22: M10.pin_1, L298N2.OUT2
  N23: M10.pin_2, L298N2.OUT1
  N24: M11.pin_1, L298N2.OUT4
  N25: M11.pin_2, L298N2.OUT3
  N26: M12.pin_1, L298N3.OUT2
  N27: M12.pin_2, L298N3.OUT1
  N28: M13.pin_1, L298N3.OUT4
  N29: M13.pin_2, L298N3.OUT3
  GND: VCC3.-, L298N1.GND, L298N2.GND, L298N3.GND
  12V: VCC3.+, L298N1.12V, L298N2.12V, L298N3.12V
  N30: L298N1.IN1, PWM1.no_name_yet#15
  N31: L298N1.IN2, PWM1.no_name_yet#14
  N32: L298N1.IN3, PWM1.no_name_yet#13
  N33: L298N1.IN4, PWM1.no_name_yet#12
  N34: L298N2.IN1, PWM1.no_name_yet#11
  N35: L298N2.IN2, PWM1.no_name_yet#10
  N36: L298N2.IN3, PWM1.no_name_yet#9
  N37: L298N2.IN4, PWM1.no_name_yet#8
  N38: L298N3.IN1, PWM1.no_name_yet#7
  N39: L298N3.IN2, PWM1.no_name_yet#6
  N40: L298N3.IN3, PWM1.no_name_yet#5
  N41: L298N3.IN4, PWM1.no_name_yet#4

custom parts:
  L298N DC motor driver: 2x DC motor driver with 78M05 positive voltage regulator (7..35 V) L298N: max 46 V, 2 A Set 5 V Enable jumper to enable 5 V regultor (needed for the L298N) and +5 V output at screw terminal or supply external +5 V at screw terminal Set ENA and/or ENB to +5 V to enable motor permanently or supply ENA and/or ENB with PWM signal IN1 and IN2 set rotation directory for motor A (OUT1/OUT2) IN2 and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
